// Logisim project trabalho completo.circ as structural Verilog: 2 circuits, main circuit main
module main (
  input  E,
  input  F,
  input  A,
  input  B,
  input  C,
  input  D,
  output ROXO,
  output VERMELHO,
  output SIRENE,
  output LARANJA
);

  wire and_1_out, and_2_out, and_3_out, and_4_out, and_5_out, not_1_out, not_2_out, not_3_out, not_4_out,
       or_2_out, or_3_out, or_4_out, or_5_out, or_7_out, or_8_out;

  or or_1 (ROXO, E, F);
  or or_2 (or_2_out, E, F, A);
  or or_3 (or_3_out, E, F, B);
  or or_4 (or_4_out, E, F, C);
  or or_5 (or_5_out, E, F, D);
  not not_1 (not_1_out, or_3_out);
  not not_2 (not_2_out, or_5_out);
  buf or_6 (VERMELHO, F);  // OR_Gate
  not not_3 (not_3_out, or_2_out);
  not not_4 (not_4_out, or_3_out);
  and and_1 (and_1_out, or_2_out, not_1_out);
  and and_2 (and_2_out, not_3_out, not_4_out);
  and and_3 (and_3_out, not_4_out, or_4_out);
  and and_4 (and_4_out, and_2_out, or_5_out);
  or or_7 (or_7_out, and_1_out, or_8_out, or_3_out);
  and and_5 (and_5_out, and_3_out, not_2_out);
  or or_8 (or_8_out, and_4_out, and_5_out);
  and and_6 (SIRENE, ROXO, LARANJA, VERMELHO);
  or or_9 (LARANJA, E, F, or_7_out);
endmodule

module SIRENE (
  input  E,
  input  F,
  input  A,
  input  B,
  input  C,
  input  D,
  output LED_ROXO,
  output LED_VERMELHO,
  output SIRENE,
  output LED_LARANJA
);

  wire and_1_out, and_2_out, and_3_out, nor_1_out, nor_2_out, nor_3_out, nor_4_out, nor_5_out, or_2_out,
       or_3_out, or_4_out;

  or or_1 (LED_ROXO, E, F);
  nor nor_1 (nor_1_out, E, F, A);
  nor nor_2 (nor_2_out, E, F, B);
  or or_2 (or_2_out, E, F, D);
  nor nor_3 (nor_3_out, E, F, B);
  or or_3 (or_3_out, E, F, C);
  nor nor_4 (nor_4_out, E, F, D);
  or or_4 (or_4_out, E, F, A);
  nor nor_5 (nor_5_out, E, F, B);
  and and_1 (and_1_out, nor_1_out, nor_2_out, or_2_out);
  and and_2 (and_2_out, nor_3_out, or_3_out, nor_4_out);
  and and_3 (and_3_out, or_4_out, nor_5_out);
  or or_5 (LED_LARANJA, E, F, and_1_out, and_2_out, and_3_out, E, F, B);
  and and_4 (SIRENE, LED_ROXO, LED_LARANJA, F);

  assign LED_VERMELHO = F;
endmodule
